# Fritzing sketch schematics (saved by Fritzing 0.9.4)
breadboards: 1

parts:
  Part1 = Arduino Uno (Rev3)
  R1 = Resistor [tolerance=±5% resistance=220 package=THT]
  R2 = Resistor [tolerance=±5% resistance=220 package=THT]
  R3 = Resistor [tolerance=±5% resistance=220 package=THT]
  7_Segment1 = 7 Segment Display
  DHT1 = DHT22 Humidity and Temperature Sensor
  7_Segment2 = 7 Segment Display
  R4 = Resistor [tolerance=±5% resistance=220 package=THT]
  R5 = Resistor [tolerance=±5% resistance=10k package=THT]

nets:
  N1: Part1.A0, DHT1.NULL
  N2: Part1.D8, 7_Segment2.Segment_DP
  N3: Part1.D9_PWM, 7_Segment2.Segment_E
  N4: Part1.D10_PWM/SS, 7_Segment2.Segment_F
  N5: Part1.D11_PWM/MOSI, 7_Segment2.Segment_G
  N6: Part1.D12/MISO, 7_Segment2.Segment_B
  N7: Part1.D13/SCK, 7_Segment2.Segment_A
  N8: Part1.D0/RX, 7_Segment1.Segment_C
  N9: Part1.D1/TX, 7_Segment1.Segment_DP
  N10: Part1.D2, R1.Pin_0, 7_Segment1.Segment_E
  N11: Part1.D3_PWM, 7_Segment1.Segment_F
  N12: Part1.D4, 7_Segment1.Segment_G
  N13: Part1.D5_PWM, 7_Segment1.Segment_B
  N14: Part1.D6_PWM, 7_Segment1.Segment_A
  N15: Part1.D7, 7_Segment2.Segment_C
  N16: Part1.5V, DHT1.DATA, R5.Pin_0, R5.Pin_1
  GND: Part1.GND, R2.Pin_1, R3.Pin_1, DHT1.GND
  N17: R2.Pin_0, 7_Segment1.common_anode, R4.Pin_1
  N18: R3.Pin_0, 7_Segment2.common_anode
